// Logisim project LC-2200-16.circ as structural Verilog: 3 circuits, main circuit main
module main (
  output [5:0] addhceck
);

  wire ALUHi, ALULo, and_1_out, Clock, comparator_1_eq, comparator_2_eq, DrALU, DrMEM, DrOFF, DrPC, DrREG,
       LdA, LdB, LdIR, LdMAR, LdPC, LdZ, nand_1_out, not_1_out, not_2_out, RegSelHi, RegSelLo, WrMEM, WrREG,
       Z;
  wire [3:0] multiplexer_1_out, RX, RY, RZ;
  wire [15:0] A_q, alu_1_output, B_q, bit_extender_1_out, controlled_buffer_1_out, IR_q, MAR_q, PC_q,
       ram_1_data, ram_2_data;

  Clock clock_1 (.out(Clock));
  Register #(.width(16)) PC (.D(controlled_buffer_1_out), .en(LdPC), .Q(PC_q), .clk(Clock));  // open: clr
  assign controlled_buffer_1_out = DrPC ? PC_q : 16'bz;  // Controlled_Buffer controlled_buffer_1
  Register #(.width(16)) A (.D(controlled_buffer_1_out), .en(LdA), .Q(A_q), .clk(Clock));  // open: clr
  ALU alu_1 (.A(A_q), .B(B_q), .func({ALUHi, ALULo}), .Output(alu_1_output));
  Comparator #(.width(4)) comparator_1 (.a(multiplexer_1_out), .b(4'b0000), .eq(comparator_1_eq));  // open: gt, lt
  assign controlled_buffer_1_out = DrALU ? alu_1_output : 16'bz;  // Controlled_Buffer controlled_buffer_2
  Comparator #(.width(16)) comparator_2 (
    .a(controlled_buffer_1_out), .b({16{1'b0}}), .eq(comparator_2_eq));  // open: gt, lt
  Register #(.width(1)) register_1 (.D(comparator_2_eq), .en(LdZ), .Q(Z), .clk(Clock));  // open: clr
  Register #(.width(16)) B (.D(controlled_buffer_1_out), .en(LdB), .Q(B_q), .clk(Clock));  // open: clr
  and and_1 (and_1_out, nand_1_out, WrREG);
  nand nand_1 (nand_1_out, comparator_1_eq, WrREG);
  Multiplexer #(.select(2), .width(4)) multiplexer_1 (
    .in0(RX), .in1(RY), .in2(RZ), .out(multiplexer_1_out), .sel({RegSelHi, RegSelLo}), .en(1'b1));  // open: in3
  assign controlled_buffer_1_out = DrREG ? ram_1_data : 16'bz;  // Controlled_Buffer controlled_buffer_3
  not not_1 (not_1_out, WrREG);
  RAM #(.addrWidth(4), .dataWidth(16), .bus("separate")) ram_1 (
    .addr(multiplexer_1_out), .din(controlled_buffer_1_out), .data(ram_1_data), .str(and_1_out), .clk(Clock),
    .ld(not_1_out));  // open: sel, clr
  Register #(.width(16)) MAR (.D(controlled_buffer_1_out), .en(LdMAR), .Q(MAR_q), .clk(Clock));  // open: clr
  assign controlled_buffer_1_out = DrMEM ? ram_2_data : 16'bz;  // Controlled_Buffer controlled_buffer_4
  RAM #(.addrWidth(16), .dataWidth(16), .bus("separate")) ram_2 (
    .addr(MAR_q), .din(controlled_buffer_1_out), .data(ram_2_data), .str(WrMEM), .clk(Clock), .ld(not_2_out));  // open: sel, clr
  not not_2 (not_2_out, WrMEM);
  assign controlled_buffer_1_out = DrOFF ? bit_extender_1_out : 16'bz;  // Controlled_Buffer controlled_buffer_5
  Register #(.width(16)) IR (
    .D(controlled_buffer_1_out), .en(LdIR), .Q({IR_q[15:13], RX, RY, RZ, IR_q[0]}), .clk(Clock));  // open: clr
  assign bit_extender_1_out = {{11{RZ[3]}}, {RZ, IR_q[0]}};  // Bit_Extender bit_extender_1
  Microcontroller microcontroller_1 (
    .Z(Z), .DrREG(DrREG), .DrMEM(DrMEM), .DrALU(DrALU), .DrPC(DrPC), .DrOFF(DrOFF), .LdPC(LdPC), .LdIR(LdIR),
    .LdMAR(LdMAR), .LdA(LdA), .LdB(LdB), .LdZ(LdZ), .WrREG(WrREG), .WrMEM(WrMEM), .RegSelLo(RegSelLo),
    .RegSelHi(RegSelHi), .ALULo(ALULo), .ALUHi(ALUHi), .OpCode(IR_q[15:13]), .Clock(Clock),
    .addcheck(addhceck));

  // Notes on the sheet:
  //   SPRING 2016
endmodule

module ALU (
  input  [15:0] A,
  input  [15:0] B,
  input  [1:0] func,
  output [15:0] Output
);

  wire [15:0] adder_1_out, adder_2_out, nand_1_out, subtractor_1_out;

  Adder #(.width(16)) adder_1 (.a(A), .b(B), .out(adder_1_out));  // open: cin, cout
  assign nand_1_out = ~(A & B);  // NAND_Gate nand_1, 16 bits wide
  Subtractor #(.width(16)) subtractor_1 (.a(A), .b(B), .out(subtractor_1_out));  // open: bin, bout
  Adder #(.width(16)) adder_2 (.a(A), .b(16'h1), .out(adder_2_out));  // open: cin, cout
  Multiplexer #(.select(2), .width(16)) multiplexer_1 (
    .in0(adder_1_out), .in1(nand_1_out), .in2(subtractor_1_out), .in3(adder_2_out), .out(Output), .sel(func),
    .en(1'b1));
endmodule

module Microcontroller (
  input  [2:0] OpCode,
  input  Clock,
  input  Z,
  output DrREG,
  output DrMEM,
  output DrALU,
  output DrPC,
  output DrOFF,
  output LdPC,
  output LdIR,
  output LdMAR,
  output LdA,
  output LdB,
  output LdZ,
  output WrREG,
  output WrMEM,
  output RegSelLo,
  output RegSelHi,
  output ALULo,
  output ALUHi,
  output [5:0] addcheck
);

  wire [5:0] register_1_q, rom_2_data, rom_3_data;
  wire [24:0] rom_1_data;

  ROM #(.addrWidth(6), .dataWidth(25)) rom_1 (
    .addr(register_1_q),
    .data({rom_1_data[24:23], ALUHi, ALULo, RegSelHi, RegSelLo, WrMEM, WrREG, LdZ, LdB, LdA, LdMAR, LdIR, LdPC, DrOFF, DrPC, DrALU, DrMEM, DrREG, rom_1_data[5:0]}));  // open: sel
  Register #(.width(6)) register_1 (.D(addcheck), .en(1'b1), .Q(register_1_q), .clk(Clock), .clr(1'b0));
  Multiplexer #(.select(2), .width(6)) multiplexer_1 (
    .in0(rom_1_data[5:0]), .in1(rom_2_data), .in2(rom_3_data), .out(addcheck), .sel(rom_1_data[24:23]),
    .en(1'b1));  // open: in3
  ROM #(.addrWidth(3), .dataWidth(6)) rom_2 (.addr(OpCode), .data(rom_2_data));  // open: sel
  ROM #(.addrWidth(2), .dataWidth(6)) rom_3 (.addr({1'b0, Z}), .data(rom_3_data));  // open: sel

  // Notes on the sheet:
  //   contents of rom_1 (hex, n*v repeats v):
  //   6201 1082 e00900 84044 108045 20100 8c047 204108 620100 8404a 840b 20100 8404d 840e 210f 20080 84051
  //   8412 2113 40040 4055 88056 41011d 4218 8419 900 a021b 840 1c 1000000
  //   contents of rom_2 (hex, n*v repeats v):
  //   3 6 9 c 10 14 1a 1c
  //   contents of rom_3 (hex, n*v repeats v):
  //   0 17
endmodule
