// Logisim project Lesniak_Joseph.circ as structural Verilog: 11 circuits, main circuit main
module main (
);

  wire _0, _2ndReg, and_1_out, and_2_out, and_3_out, B, CheckA, CheckB, Clock, comparator_1_eq,
       comparator_2_eq, comparator_3_eq, comparator_4_eq, Jump, Jumping, LdMEM, not_1_out, not_2_out,
       or_1_out, RegToWr, Rep_REGNO1, Rep_REGNO2, Stall, StallR, WrEN, WrMEM;
  wire [1:0] ALU_Func, NextInst, REGData;
  wire [2:0] idrr_ex_buffer_1_opcode_out, multiplexer_9_out, Opcode_MEM, Opcode_WB, OpcodeEX;
  wire [3:0] BToCheck, LWWrReg, multiplexer_6_out, RegToWr_In_EX, RegToWr_In_IDRR, RegToWr_In_MEM, WrREGNO;
  wire [7:0] PC_q, PC_q_2, PC_q_3, PC_q_4;
  wire [31:0] _2ndRegCont, _2ndRegCont_EX, _2ndRegCont_MEM, A_EX, ALU_MEM, ALU_Out, ALU_WB, B_EX, BCont_IDRR,
       BEQ_Add, Data_For_REGNO1, Data_For_REGNO2, dual_ported_register_file_1_out1,
       dual_ported_register_file_1_out2, INPUT, InstructionIDRR, InstructionIF, MEMData, MEMData_WB,
       multiplexer_1_out, multiplexer_2_out, Offset_EX, OffsetIDRR, PC_1, PC_1_EX, PC_1_MEM, PC_1_WB,
       PC_1IDRR, RYCont;

  Register #(.width(32)) PC (
    .D(multiplexer_1_out), .en(not_1_out), .Q({PC_q, PC_q_4, PC_q_3, PC_q_2}), .clk(Clock));  // open: clr
  not not_1 (not_1_out, Stall);
  Clock clock_1 (.out(Clock));
  Multiplexer #(.select(2), .width(32)) multiplexer_1 (
    .in0(PC_1), .in1(BEQ_Add), .in2(_2ndRegCont_EX), .out(multiplexer_1_out), .sel(NextInst), .en(1'b1));  // open: in3
  Adder #(.width(32)) adder_1 (.a({PC_q, PC_q_4, PC_q_3, PC_q_2}), .b(32'h1), .out(PC_1));  // open: cin, cout
  ROM #(.addrWidth(24), .dataWidth(32)) rom_1 (.addr({PC_q_4, PC_q_3, PC_q_2}), .data(InstructionIF));  // open: sel
  Multiplexer #(.width(32)) multiplexer_2 (
    .in0(InstructionIF), .in1({32{1'b0}}), .out(multiplexer_2_out), .sel(Jumping), .en(1'b1));
  IF_IDRR_Buffer if_idrr_buffer_1 (
    .Instruction_In(multiplexer_2_out), .PC_In(PC_1), .Instruction_Out(InstructionIDRR), .PC_Out(PC_1IDRR),
    .Clock(Clock), .StallBit(Stall));
  Stalling_Unit stalling_unit_1 (.OpCodeIn(InstructionIDRR[30:28]), .CheckA(CheckA), .CheckB(CheckB));
  Multiplexer #(.width(4)) multiplexer_3 (
    .in0(InstructionIDRR[27:24]), .in1(InstructionIDRR[3:0]), .out(BToCheck), .sel(_2ndReg), .en(1'b1));
  Comparator #(.width(4)) comparator_1 (.a(LWWrReg), .b(4'b0000), .eq(comparator_1_eq));  // open: gt, lt
  assign OffsetIDRR = {{12{InstructionIDRR[19]}}, InstructionIDRR[19:0]};  // Bit_Extender bit_extender_1
  ROM #(.addrWidth(3), .dataWidth(3)) rom_2 (.addr(InstructionIDRR[30:28]), .data({RegToWr, B, _2ndReg}));  // open: sel
  Comparator #(.width(4), .mode("unsigned")) comparator_2 (
    .a(InstructionIDRR[23:20]), .b(LWWrReg), .eq(comparator_2_eq));  // open: gt, lt
  Comparator #(.width(4), .mode("unsigned")) comparator_3 (
    .a(BToCheck), .b(LWWrReg), .eq(comparator_3_eq));  // open: gt, lt
  Dual_Ported_Register_File dual_ported_register_file_1 (
    .CLK(Clock), .WrREGNO(WrREGNO), .RdREGNO1(InstructionIDRR[23:20]), .RdREGNO2(BToCheck), .INPUT(INPUT),
    .OUT1(dual_ported_register_file_1_out1), .OUT2(dual_ported_register_file_1_out2), .WrEN(WrEN));
  Multiplexer #(.width(32)) multiplexer_4 (.in0(_2ndRegCont), .in1(OffsetIDRR), .out(BCont_IDRR), .sel(B), .en(1'b1));
  Multiplexer #(.width(4)) multiplexer_5 (
    .in0(InstructionIDRR[27:24]), .in1(InstructionIDRR[23:20]), .out(RegToWr_In_IDRR), .sel(RegToWr),
    .en(1'b1));
  Comparator #(.width(3)) comparator_4 (.a(InstructionIDRR[30:28]), .b(3'b011), .eq(comparator_4_eq));  // open: gt, lt
  and and_1 (and_1_out, comparator_2_eq, CheckA);
  and and_2 (and_2_out, comparator_3_eq, CheckB);
  Register #(.width(4)) register_1 (.D(multiplexer_6_out), .en(1'b1), .Q(LWWrReg), .clk(Clock));  // open: clr
  Multiplexer #(.width(4)) multiplexer_6 (
    .in0(4'b0000), .in1(InstructionIDRR[27:24]), .out(multiplexer_6_out), .sel(comparator_4_eq), .en(1'b1));
  or or_1 (or_1_out, and_1_out, and_2_out);
  and and_3 (and_3_out, or_1_out, not_2_out);
  not not_2 (not_2_out, comparator_1_eq);
  Multiplexer #(.width(32)) multiplexer_7 (
    .in0(dual_ported_register_file_1_out1), .in1(Data_For_REGNO1), .out(RYCont), .sel(Rep_REGNO1), .en(1'b1));
  Multiplexer #(.width(32)) multiplexer_8 (
    .in0(dual_ported_register_file_1_out2), .in1(Data_For_REGNO2), .out(_2ndRegCont), .sel(Rep_REGNO2),
    .en(1'b1));
  Register #(.width(1), .trigger("falling")) register_2 (
    .D(and_3_out), .en(1'b1), .Q(Stall), .clk(Clock));  // open: clr
  Register #(.width(1)) register_3 (.D(and_3_out), .en(1'b1), .Q(StallR), .clk(Clock));  // open: clr
  Multiplexer #(.width(3)) multiplexer_9 (
    .in0(InstructionIDRR[30:28]), .in1(3'b111), .out(multiplexer_9_out), .sel(Jumping), .en(1'b1));
  Multiplexer #(.width(3)) multiplexer_10 (
    .in0(idrr_ex_buffer_1_opcode_out), .in1(3'b111), .out(OpcodeEX), .sel(StallR), .en(1'b1));
  IDRR_EX_Buffer idrr_ex_buffer_1 (
    .Clock(Clock), .RegToWr_In(RegToWr_In_IDRR), .RegToWr_Out(RegToWr_In_EX), .A_In(RYCont), .A_Out(A_EX),
    .Rx_Contents_In(_2ndRegCont), .Rx_Contents_Out(_2ndRegCont_EX), .PC_In(PC_1IDRR), .PC_Out(PC_1_EX),
    .B_In(BCont_IDRR), .B_Out(B_EX), .Off_In(OffsetIDRR), .Off_Out(Offset_EX), .StallBit(Stall),
    .Opcode_In(multiplexer_9_out), .Opcode_Out(idrr_ex_buffer_1_opcode_out));
  Forwarding_Unit forwarding_unit_1 (
    .REGNO1(InstructionIDRR[23:20]), .REGNO2(BToCheck), .WrREG_EX(RegToWr_In_EX), .WrREG_MEM(RegToWr_In_MEM),
    .WrREG_WB(WrREGNO), .EX_ALU(ALU_Out), .EX_PC_1(PC_1_EX), .MEM_ALU(ALU_MEM), .MEM_Data(MEMData),
    .MEM_PC_1(PC_1_MEM), .WB_ALU(ALU_WB), .WB_MEM(MEMData_WB), .WB_PC_1(PC_1_WB), .Opcode_EX(OpcodeEX),
    .Opcode_MEM(Opcode_MEM), .Opcode_WB(Opcode_WB), .Data_For_REGNO1(Data_For_REGNO1),
    .Replace_REGNO1(Rep_REGNO1), .Replace_REGNO2(Rep_REGNO2), .Data_For_REGNO2(Data_For_REGNO2));
  Adder #(.width(32)) adder_2 (.a(PC_1_EX), .b(Offset_EX), .out(BEQ_Add));  // open: cin, cout
  Comparator #(.width(2), .mode("unsigned")) comparator_5 (.a(NextInst), .b(2'b00), .gt(Jumping));  // open: eq, lt
  Next_Instruction next_instruction_1 (._0(_0), .Func(ALU_Func), .Jump(Jump), .NextInst(NextInst));
  Comparator #(.width(32), .mode("unsigned")) comparator_6 (.a(ALU_Out), .b({32{1'b0}}), .eq(_0));  // open: gt, lt
  ROM #(.addrWidth(3), .dataWidth(3)) rom_3 (.addr(OpcodeEX), .data({Jump, ALU_Func}));  // open: sel
  ALU alu_1 (.FUNC(ALU_Func), .A(A_EX), .B(B_EX), .OUT(ALU_Out));
  EX_MEM_Buffer ex_mem_buffer_1 (
    .RegToWr_In(RegToWr_In_EX), .ALU_In(ALU_Out), .DataToWrMem_In(_2ndRegCont_EX), .PC_In(PC_1_EX),
    .RegToWr_Out(RegToWr_In_MEM), .ALU_Out(ALU_MEM), .DataToWrMem_Out(_2ndRegCont_MEM), .PC_Out(PC_1_MEM),
    .Clock(Clock), .Opcode_In(OpcodeEX), .Opcode_Out(Opcode_MEM));
  RAM #(.addrWidth(24), .dataWidth(32), .bus("separate")) ram_1 (
    .addr(ALU_MEM[23:0]), .din(_2ndRegCont_MEM), .data(MEMData), .str(WrMEM), .clk(Clock), .ld(LdMEM));  // open: sel, clr
  ROM #(.addrWidth(3), .dataWidth(2)) rom_4 (.addr(Opcode_MEM), .data({WrMEM, LdMEM}));  // open: sel
  MEM_WB_Buffer mem_wb_buffer_1 (
    .RegToWr_In(RegToWr_In_MEM), .ALU_In(ALU_MEM), .D_MEM_In(MEMData), .RegToWr_Out(WrREGNO),
    .ALU_Out(ALU_WB), .D_MEM_Out(MEMData_WB), .Clock(Clock), .PC_In(PC_1_MEM), .PC_Out(PC_1_WB),
    .Opcode_In(Opcode_MEM), .Opcode_Out(Opcode_WB));
  Multiplexer #(.select(2), .width(32)) multiplexer_11 (
    .in0(ALU_WB), .in1(MEMData_WB), .in2(PC_1_WB), .out(INPUT), .sel(REGData), .en(1'b1));  // open: in3
  ROM #(.addrWidth(3), .dataWidth(3)) rom_5 (.addr(Opcode_WB), .data({REGData, WrEN}));  // open: sel

  // Other names for the same wires on the sheet: RZ[3:0] = InstructionIDRR[3:0]; RY[3:0] = InstructionIDRR[23:20];
  //   RX[3:0] = InstructionIDRR[27:24]; OpcodeIDRR[2:0] = InstructionIDRR[30:28]; JALR_Add[31:0] = _2ndRegCont_EX

  // Notes on the sheet:
  //   contents of rom_1 (hex, n*v repeats v):
  //   2800000a 40000000 23300001 43000010 53800001 500ffffc 34000000 24400001 44000000 54800001 500ffffb
  //   contents of rom_2 (hex, n*v repeats v):
  //   1 1 2 2 2 0 4
  //   contents of rom_3 (hex, n*v repeats v):
  //   0 1 0 0 0 2 4
  //   contents of rom_4 (hex, n*v repeats v):
  //   0 0 0 1 2
  //   contents of rom_5 (hex, n*v repeats v):
  //   1 1 1 3 0 0 5
endmodule

module Dual_Ported_Register_File (
  input  CLK,
  input  WrEN,
  input  [3:0] WrREGNO,
  input  [3:0] RdREGNO1,
  input  [3:0] RdREGNO2,
  input  [31:0] INPUT,
  output [31:0] OUT1,
  output [31:0] OUT2
);

  wire En_a0, En_a1, En_a2, En_a3, En_a4, En_at, En_fp, En_k0, En_ra, En_s0, En_s1, En_s2, En_s3, En_sp,
       En_v0;
  wire [31:0] a0, a1, a2, a3, a4, at, fp, k0, ra, s0, s1, s2, s3, sp, v0, zero;

  Decoder #(.select(4), .disabled(0)) decoder_1 (
    .out1(En_at), .out2(En_v0), .out3(En_a0), .out4(En_a1), .out5(En_a2), .out6(En_a3), .out7(En_a4),
    .out8(En_s0), .out9(En_s1), .out10(En_s2), .out11(En_s3), .out12(En_k0), .out13(En_sp), .out14(En_fp),
    .out15(En_ra), .sel(WrREGNO), .en(WrEN));  // open: out0
  Register #(.width(32)) u_zero (.D(INPUT), .en(1'b0), .Q(zero), .clk(CLK));  // open: clr
  Register #(.width(32)) u_at (.D(INPUT), .en(En_at), .Q(at), .clk(CLK));  // open: clr
  Register #(.width(32)) u_v0 (.D(INPUT), .en(En_v0), .Q(v0), .clk(CLK));  // open: clr
  Register #(.width(32)) u_a0 (.D(INPUT), .en(En_a0), .Q(a0), .clk(CLK));  // open: clr
  Register #(.width(32)) u_a1 (.D(INPUT), .en(En_a1), .Q(a1), .clk(CLK));  // open: clr
  Register #(.width(32)) u_a2 (.D(INPUT), .en(En_a2), .Q(a2), .clk(CLK));  // open: clr
  Register #(.width(32)) u_a3 (.D(INPUT), .en(En_a3), .Q(a3), .clk(CLK));  // open: clr
  Register #(.width(32)) u_a4 (.D(INPUT), .en(En_a4), .Q(a4), .clk(CLK));  // open: clr
  Multiplexer #(.select(4), .width(32), .disabled(0), .enable("false")) multiplexer_1 (
    .in0(zero), .in1(at), .in2(v0), .in3(a0), .in4(a1), .in5(a2), .in6(a3), .in7(a4), .in8(s0), .in9(s1),
    .in10(s2), .in11(s3), .in12(k0), .in13(sp), .in14(fp), .in15(ra), .out(OUT2), .sel(RdREGNO2));
  Register #(.width(32)) u_s0 (.D(INPUT), .en(En_s0), .Q(s0), .clk(CLK));  // open: clr
  Register #(.width(32)) u_s1 (.D(INPUT), .en(En_s1), .Q(s1), .clk(CLK));  // open: clr
  Register #(.width(32)) u_s2 (.D(INPUT), .en(En_s2), .Q(s2), .clk(CLK));  // open: clr
  Register #(.width(32)) u_s3 (.D(INPUT), .en(En_s3), .Q(s3), .clk(CLK));  // open: clr
  Register #(.width(32)) u_k0 (.D(INPUT), .en(En_k0), .Q(k0), .clk(CLK));  // open: clr
  Register #(.width(32)) u_sp (.D(INPUT), .en(En_sp), .Q(sp), .clk(CLK));  // open: clr
  Register #(.width(32)) u_fp (.D(INPUT), .en(En_fp), .Q(fp), .clk(CLK));  // open: clr
  Register #(.width(32)) u_ra (.D(INPUT), .en(En_ra), .Q(ra), .clk(CLK));  // open: clr
  Multiplexer #(.select(4), .width(32), .disabled(0), .enable("false")) multiplexer_2 (
    .in0(zero), .in1(at), .in2(v0), .in3(a0), .in4(a1), .in5(a2), .in6(a3), .in7(a4), .in8(s0), .in9(s1),
    .in10(s2), .in11(s3), .in12(k0), .in13(sp), .in14(fp), .in15(ra), .out(OUT1), .sel(RdREGNO1));

  // Notes on the sheet:
  //   MODIFY AT YOUR OWN RISK
endmodule

module IF_IDRR_Buffer (
  input  [31:0] Instruction_In,
  input  StallBit,
  input  Clock,
  input  [31:0] PC_In,
  output [31:0] Instruction_Out,
  output [31:0] PC_Out
);

  wire not_1_out;

  not not_1 (not_1_out, StallBit);
  Register #(.width(32)) register_1 (
    .D(Instruction_In), .en(not_1_out), .Q(Instruction_Out), .clk(Clock));  // open: clr
  Register #(.width(32)) register_2 (.D(PC_In), .en(not_1_out), .Q(PC_Out), .clk(Clock));  // open: clr
endmodule

module IDRR_EX_Buffer (
  input  Clock,
  input  [2:0] Opcode_In,
  input  [3:0] RegToWr_In,
  input  [31:0] A_In,
  input  [31:0] B_In,
  input  StallBit,
  input  [31:0] Rx_Contents_In,
  input  [31:0] PC_In,
  input  [31:0] Off_In,
  output [2:0] Opcode_Out,
  output [3:0] RegToWr_Out,
  output [31:0] A_Out,
  output [31:0] B_Out,
  output [31:0] Rx_Contents_Out,
  output [31:0] PC_Out,
  output [31:0] Off_Out
);

  wire not_1_out;

  not not_1 (not_1_out, StallBit);
  Register #(.width(3)) register_1 (.D(Opcode_In), .en(not_1_out), .Q(Opcode_Out), .clk(Clock));  // open: clr
  Register #(.width(4)) register_2 (.D(RegToWr_In), .en(not_1_out), .Q(RegToWr_Out), .clk(Clock));  // open: clr
  Register #(.width(32)) register_3 (.D(A_In), .en(not_1_out), .Q(A_Out), .clk(Clock));  // open: clr
  Register #(.width(32)) register_4 (.D(B_In), .en(not_1_out), .Q(B_Out), .clk(Clock));  // open: clr
  Register #(.width(32)) register_5 (
    .D(Rx_Contents_In), .en(not_1_out), .Q(Rx_Contents_Out), .clk(Clock));  // open: clr
  Register #(.width(32)) register_6 (.D(PC_In), .en(not_1_out), .Q(PC_Out), .clk(Clock));  // open: clr
  Register #(.width(32)) register_7 (.D(Off_In), .en(not_1_out), .Q(Off_Out), .clk(Clock));  // open: clr
endmodule

module EX_MEM_Buffer (
  input  Clock,
  input  [2:0] Opcode_In,
  input  [3:0] RegToWr_In,
  input  [31:0] ALU_In,
  input  [31:0] DataToWrMem_In,
  input  [31:0] PC_In,
  output [2:0] Opcode_Out,
  output [3:0] RegToWr_Out,
  output [31:0] ALU_Out,
  output [31:0] DataToWrMem_Out,
  output [31:0] PC_Out
);

  Register #(.width(3)) register_1 (.D(Opcode_In), .en(1'b1), .Q(Opcode_Out), .clk(Clock));  // open: clr
  Register #(.width(4)) register_2 (.D(RegToWr_In), .en(1'b1), .Q(RegToWr_Out), .clk(Clock));  // open: clr
  Register #(.width(32)) register_3 (.D(ALU_In), .en(1'b1), .Q(ALU_Out), .clk(Clock));  // open: clr
  Register #(.width(32)) register_4 (.D(DataToWrMem_In), .en(1'b1), .Q(DataToWrMem_Out), .clk(Clock));  // open: clr
  Register #(.width(32)) register_5 (.D(PC_In), .en(1'b1), .Q(PC_Out), .clk(Clock));  // open: clr
endmodule

module MEM_WB_Buffer (
  input  Clock,
  input  [2:0] Opcode_In,
  input  [3:0] RegToWr_In,
  input  [31:0] ALU_In,
  input  [31:0] D_MEM_In,
  input  [31:0] PC_In,
  output [2:0] Opcode_Out,
  output [3:0] RegToWr_Out,
  output [31:0] ALU_Out,
  output [31:0] D_MEM_Out,
  output [31:0] PC_Out
);

  Register #(.width(3)) register_1 (.D(Opcode_In), .en(1'b1), .Q(Opcode_Out), .clk(Clock));  // open: clr
  Register #(.width(4)) register_2 (.D(RegToWr_In), .en(1'b1), .Q(RegToWr_Out), .clk(Clock));  // open: clr
  Register #(.width(32)) register_3 (.D(ALU_In), .en(1'b1), .Q(ALU_Out), .clk(Clock));  // open: clr
  Register #(.width(32)) register_4 (.D(D_MEM_In), .en(1'b1), .Q(D_MEM_Out), .clk(Clock));  // open: clr
  Register #(.width(32)) register_5 (.D(PC_In), .en(1'b1), .Q(PC_Out), .clk(Clock));  // open: clr
endmodule

module ALU (
  input  [1:0] FUNC,
  input  [31:0] A,
  input  [31:0] B,
  output [31:0] OUT
);

  wire [31:0] adder_1_out, adder_2_out, nand_1_out, subtractor_1_out;

  Adder #(.width(32)) adder_1 (.a(A), .b(B), .out(adder_1_out), .cin(1'b0));  // open: cout
  assign nand_1_out = ~(A & B);  // NAND_Gate nand_1, 32 bits wide
  Subtractor #(.width(32)) subtractor_1 (.a(A), .b(B), .out(subtractor_1_out), .bin(1'b0));  // open: bout
  Adder #(.width(32)) adder_2 (.a(A), .b({32{1'b0}}), .out(adder_2_out), .cin(1'b1));  // open: cout
  Multiplexer #(.select(2), .width(32), .disabled(0), .enable("false")) multiplexer_1 (
    .in0(adder_1_out), .in1(nand_1_out), .in2(subtractor_1_out), .in3(adder_2_out), .out(OUT), .sel(FUNC));

  // Notes on the sheet:
  //   MODIFY AT YOUR OWN RISK
endmodule

module Stalling_Unit (
  input  [2:0] OpCodeIn,
  output CheckA,
  output CheckB
);

  wire ADD, ADDI, BEQ, JALR, LW, NAND, SW;

  Comparator #(.width(3), .mode("unsigned")) comparator_1 (.a(OpCodeIn), .b(3'b000), .eq(ADD));  // open: gt, lt
  Comparator #(.width(3), .mode("unsigned")) comparator_2 (.a(OpCodeIn), .b(3'b001), .eq(NAND));  // open: gt, lt
  Comparator #(.width(3), .mode("unsigned")) comparator_3 (.a(OpCodeIn), .b(3'b010), .eq(ADDI));  // open: gt, lt
  Comparator #(.width(3), .mode("unsigned")) comparator_4 (.a(OpCodeIn), .b(3'b011), .eq(LW));  // open: gt, lt
  Comparator #(.width(3), .mode("unsigned")) comparator_5 (.a(OpCodeIn), .b(3'b100), .eq(SW));  // open: gt, lt
  Comparator #(.width(3), .mode("unsigned")) comparator_6 (.a(OpCodeIn), .b(3'b101), .eq(BEQ));  // open: gt, lt
  Comparator #(.width(3), .mode("unsigned")) comparator_7 (.a(OpCodeIn), .b(3'b110), .eq(JALR));  // open: gt, lt
  or or_1 (CheckA, ADD, NAND, ADDI, LW, SW, BEQ);
  or or_2 (CheckB, ADD, NAND, SW, BEQ, JALR);
endmodule

module Next_Instruction (
  input  _0,
  input  [1:0] Func,
  input  Jump,
  output [1:0] NextInst
);

  wire and_1_out, comparator_1_eq, nor_1_out;

  Comparator #(.width(2), .mode("unsigned")) comparator_1 (.a(Func), .b(2'b10), .eq(comparator_1_eq));  // open: gt, lt
  and and_1 (and_1_out, _0, comparator_1_eq);
  nor nor_1 (nor_1_out, and_1_out, Jump);
  assign NextInst = and_1_out ? 2'b01 : 2'bz;  // Controlled_Buffer controlled_buffer_1
  assign NextInst = Jump ? 2'b10 : 2'bz;  // Controlled_Buffer controlled_buffer_2
  assign NextInst = nor_1_out ? 2'b00 : 2'bz;  // Controlled_Buffer controlled_buffer_3
endmodule

module Extra (
  output [31:0] CheckA,
  output [3:0] CheckA_2
);

  wire and_1_out, and_2_out, and_3_out, B, CheckA_t, CheckB, Clock, comparator_1_eq, comparator_2_eq,
       comparator_3_eq, comparator_4_eq, comparator_5_eq, comparator_6_eq, Jump, Jumping, not_1_out,
       not_2_out, or_1_out, or_2_out, Reg2Read, RegToWr, Stall, StallR, undriven_2, undriven_3, undriven_9,
       undriven_12, undriven_13, WrEN;
  wire [1:0] Func, multiplexer_4_out, multiplexer_4_out_3, multiplexer_17_out, NextInst, undriven,
       undriven_4, undriven_16;
  wire [2:0] multiplexer_10_out, Opcode;
  wire [3:0] BToCheck, LWWrReg, multiplexer_12_out, RegToWr_In, Rx, Ry, Rz, undriven_5, WrREGNO;
  wire [8:5] multiplexer_4_out_2;
  wire [10:0] rom_2_data;
  wire [23:0] undriven_14;
  wire [31:0] adder_1_out, alu_1_out, BEQ, bit_extender_1_out, dual_ported_register_file_1_out1,
       dual_ported_register_file_1_out2, if_idrr_buffer_1_p5, if_idrr_buffer_1_p6, INPUT, JALR,
       multiplexer_1_out, multiplexer_8_out, multiplexer_13_out, multiplexer_14_out, multiplexer_18_out,
       multiplexer_20_out, PC, ram_1_data, rom_1_data, undriven_6, undriven_7, undriven_8, undriven_10,
       undriven_11, undriven_17, undriven_18, undriven_19;
  wire [31:4] if_idrr_buffer_1_p7;
  wire [31:24] undriven_15;

  Register #(.width(32)) u_PC (.D(multiplexer_1_out), .en(not_1_out), .Q(CheckA), .clk(Clock));  // open: clr
  not not_1 (not_1_out, Stall);
  Clock clock_1 (.out(Clock));
  Multiplexer #(.select(2), .width(32)) multiplexer_1 (
    .in0(adder_1_out), .in1(BEQ), .in2(JALR), .out(multiplexer_1_out), .sel(NextInst), .en(1'b1));  // open: in3
  Adder #(.width(32)) adder_1 (.a(CheckA), .b(32'h1), .out(adder_1_out));  // open: cin, cout
  ROM #(.addrWidth(24), .dataWidth(32)) rom_1 (.addr(CheckA[23:0]), .data(rom_1_data));  // open: sel
  // IF_IDRR_Buffer if_idrr_buffer_1: pin names not known; wires that end beside it: adder_1_out, rom_1_data, Stall, Clock, if_idrr_buffer_1_p5, if_idrr_buffer_1_p6, {if_idrr_buffer_1_p7[31], Opcode, Rx, Ry, if_idrr_buffer_1_p7[19:4], Rz}
  Comparator #(.width(32)) comparator_1 (
    .a({if_idrr_buffer_1_p7[31], Opcode, Rx, Ry, if_idrr_buffer_1_p7[19:4], Rz}), .b({32{1'b0}}),
    .eq(comparator_1_eq));  // open: gt, lt
  Multiplexer #(.width(32)) multiplexer_2 (
    .in0(if_idrr_buffer_1_p5), .in1({32{1'b0}}),
    .out({if_idrr_buffer_1_p7[31], Opcode, Rx, Ry, if_idrr_buffer_1_p7[19:4], Rz}), .sel(Jumping), .en(1'b1));
  Multiplexer #(.width(32)) multiplexer_3 (
    .in0(if_idrr_buffer_1_p6), .in1({32{1'b0}}), .out(PC), .sel(Jumping), .en(1'b1));
  Multiplexer #(.width(11)) multiplexer_4 (
    .in0(rom_2_data), .in1({11{1'b0}}),
    .out({multiplexer_4_out_3, multiplexer_4_out_2, multiplexer_4_out, RegToWr, B, Reg2Read}),
    .sel(comparator_1_eq), .en(1'b1));
  ROM #(.addrWidth(3), .dataWidth(11)) rom_2 (.addr(Opcode), .data(rom_2_data));  // open: sel
  Stalling_Unit stalling_unit_1 (.OpCodeIn(Opcode), .CheckA(CheckA_t), .CheckB(CheckB));
  Multiplexer #(.width(4)) multiplexer_5 (.in0(Rx), .in1(Rz), .out(BToCheck), .sel(Reg2Read), .en(1'b1));
  Comparator #(.width(3)) comparator_2 (.a(Opcode), .b(3'b011), .eq(comparator_2_eq));  // open: gt, lt
  assign bit_extender_1_out = {{12{if_idrr_buffer_1_p7[19]}}, {if_idrr_buffer_1_p7[19:4], Rz}};  // Bit_Extender bit_extender_1
  Multiplexer #(.width(4)) multiplexer_6 (.in0(Rx), .in1(Ry), .out(RegToWr_In), .sel(RegToWr), .en(1'b1));
  Multiplexer #(.width(4)) multiplexer_7 (.in0(4'b0000), .in1(Rx), .out(CheckA_2), .sel(comparator_2_eq), .en(1'b1));
  Register #(.width(4)) register_1 (.D(CheckA_2), .en(1'b1), .Q(LWWrReg), .clk(Clock));  // open: clr
  Comparator #(.width(4)) comparator_3 (.a(LWWrReg), .b(4'b0000), .eq(comparator_3_eq));  // open: gt, lt
  Dual_Ported_Register_File dual_ported_register_file_1 (
    .CLK(Clock), .WrREGNO(WrREGNO), .RdREGNO1(Ry), .RdREGNO2(BToCheck), .INPUT(INPUT),
    .OUT1(dual_ported_register_file_1_out1), .OUT2(dual_ported_register_file_1_out2), .WrEN(WrEN));
  Comparator #(.width(4), .mode("unsigned")) comparator_4 (.a(Ry), .b(LWWrReg), .eq(comparator_4_eq));  // open: gt, lt
  Comparator #(.width(4), .mode("unsigned")) comparator_5 (
    .a(BToCheck), .b(LWWrReg), .eq(comparator_5_eq));  // open: gt, lt
  Multiplexer #(.width(32)) multiplexer_8 (
    .in0(dual_ported_register_file_1_out2), .in1(bit_extender_1_out), .out(multiplexer_8_out), .sel(B),
    .en(1'b1));
  and and_1 (and_1_out, comparator_4_eq, CheckA_t);
  and and_2 (and_2_out, comparator_5_eq, CheckB);
  or or_1 (or_1_out, and_1_out, and_2_out);
  and and_3 (and_3_out, or_1_out, not_2_out);
  not not_2 (not_2_out, comparator_3_eq);
  Multiplexer #(.width(2)) multiplexer_9 (.in0(undriven), .in1(2'b00), .out(Func), .sel(StallR), .en(1'b1));
  Multiplexer multiplexer_10 (.in0(undriven_3), .in1(1'b0), .out(multiplexer_10_out[0]), .sel(StallR), .en(1'b1));
  Multiplexer multiplexer_11 (.in0(undriven_9), .in1(1'b0), .out(multiplexer_10_out[2]), .sel(StallR), .en(1'b1));
  Multiplexer #(.width(4)) multiplexer_12 (
    .in0(undriven_5), .in1(4'b0000), .out(multiplexer_12_out), .sel(StallR), .en(1'b1));
  Multiplexer #(.width(32)) multiplexer_13 (
    .in0(undriven_10), .in1({32{1'b0}}), .out(multiplexer_13_out), .sel(StallR), .en(1'b1));
  Multiplexer #(.width(32)) multiplexer_14 (
    .in0(undriven_7), .in1({32{1'b0}}), .out(multiplexer_14_out), .sel(StallR), .en(1'b1));
  or or_2 (or_2_out, and_3_out, Jumping);
  Register #(.width(1), .trigger("falling")) register_2 (
    .D(and_3_out), .en(1'b1), .Q(Stall), .clk(Clock));  // open: clr
  Multiplexer multiplexer_15 (.in0(undriven_2), .in1(1'b0), .out(Jump), .sel(StallR), .en(1'b1));
  Multiplexer multiplexer_16 (.in0(undriven_12), .in1(1'b0), .out(multiplexer_10_out[1]), .sel(StallR), .en(1'b1));
  Multiplexer #(.width(2)) multiplexer_17 (
    .in0(undriven_4), .in1(2'b00), .out(multiplexer_17_out), .sel(StallR), .en(1'b1));
  Multiplexer #(.width(32)) multiplexer_18 (
    .in0(undriven_11), .in1({32{1'b0}}), .out(multiplexer_18_out), .sel(StallR), .en(1'b1));
  Multiplexer #(.width(32)) multiplexer_19 (.in0(undriven_6), .in1({32{1'b0}}), .out(JALR), .sel(StallR), .en(1'b1));
  Multiplexer #(.width(32)) multiplexer_20 (
    .in0(undriven_8), .in1({32{1'b0}}), .out(multiplexer_20_out), .sel(StallR), .en(1'b1));
  Register #(.width(1)) register_3 (.D(or_2_out), .en(1'b1), .Q(StallR), .clk(Clock));  // open: clr
  Adder #(.width(32)) adder_2 (.a(multiplexer_14_out), .b(multiplexer_20_out), .out(BEQ));  // open: cin, cout
  Next_Instruction next_instruction_1 (._0(comparator_6_eq), .Func(Func), .Jump(Jump), .NextInst(NextInst));
  Comparator #(.width(32)) comparator_6 (.a(alu_1_out), .b({32{1'b0}}), .eq(comparator_6_eq));  // open: gt, lt
  ALU alu_1 (.FUNC(Func), .A(multiplexer_18_out), .B(multiplexer_13_out), .OUT(alu_1_out));
  Comparator #(.width(2), .mode("unsigned")) comparator_7 (.a(NextInst), .b(2'b00), .gt(Jumping));  // open: eq, lt
  RAM #(.addrWidth(24), .dataWidth(32), .bus("separate")) ram_1 (
    .addr(undriven_14), .din({undriven_15, undriven_14}), .data(ram_1_data), .str(undriven_13), .clk(Clock),
    .ld(undriven_14[0]));  // open: sel, clr
  Multiplexer #(.select(2), .width(32)) multiplexer_21 (
    .in0(undriven_17), .in1(undriven_18), .in2(undriven_19), .out(INPUT), .sel(undriven_16), .en(1'b1));  // open: in3
  // Pins of 1 and 24 and 32 bits meet at {undriven_15, undriven_14}

  // Notes on the sheet:
  //   contents of rom_1 (hex, n*v repeats v):
  //   23000007 4*0 2800000b 4*0 68f00000 4*0 4300003
  //   contents of rom_2 (hex, n*v repeats v):
  //   101 109 102 342 82 10 524
endmodule

module Forwarding_Unit (
  input  [3:0] REGNO1,
  input  [3:0] REGNO2,
  input  [3:0] WrREG_EX,
  input  [3:0] WrREG_MEM,
  input  [3:0] WrREG_WB,
  input  [31:0] EX_ALU,
  input  [31:0] EX_PC_1,
  input  [31:0] MEM_ALU,
  input  [31:0] MEM_Data,
  input  [31:0] MEM_PC_1,
  input  [31:0] WB_ALU,
  input  [31:0] WB_MEM,
  input  [31:0] WB_PC_1,
  input  [2:0] Opcode_EX,
  input  [2:0] Opcode_MEM,
  input  [2:0] Opcode_WB,
  output Replace_REGNO1,
  output Replace_REGNO2,
  output [31:0] Data_For_REGNO1,
  output [31:0] Data_For_REGNO2
);

  wire and_1_out, and_2_out, comparator_12_eq, comparator_13_eq, nor_1_out, nor_2_out, not_1_out, not_2_out,
       not_3_out, not_4_out, not_5_out, not_6_out, not_7_out, not_8_out, not_9_out, not_10_out, not_11_out,
       not_12_out, not_13_out, not_14_out, not_15_out, not_16_out, not_17_out, not_18_out, Op_EX___4,
       Op_EX___7, Op_MEM___4, Op_MEM___7, Op_WB___4, Op_WB___7, or_1_out, or_2_out, or_3_out, or_4_out,
       or_5_out, or_6_out, or_7_out, or_8_out, REGNO1___0, REGNO1___WrREG_EX, REGNO1___WrREG_MEM,
       REGNO1___WrREG_WB, REGNO1_W__EX, REGNO1_W__MEM, REGNO1_W__WB, REGNO2___0, REGNO2___WrREG_EX,
       REGNO2___WrREG_MEM, REGNO2___WrREG_WB, REGNO2_W__EX, REGNO2_W__MEM, REGNO2_W__WB, Src_EX;
  wire [1:0] Src_MEM, Src_WB;
  wire [31:0] Data_From_EX, Data_From_MEM, Data_From_WB;

  Comparator #(.width(4), .mode("unsigned")) comparator_1 (.a(REGNO1), .b(4'b0000), .eq(REGNO1___0));  // open: gt, lt
  Comparator #(.width(4), .mode("unsigned")) comparator_2 (.a(REGNO2), .b(4'b0000), .eq(REGNO2___0));  // open: gt, lt
  Comparator #(.width(4), .mode("unsigned")) comparator_3 (
    .a(REGNO1), .b(WrREG_EX), .eq(REGNO1___WrREG_EX));  // open: gt, lt
  Comparator #(.width(4), .mode("unsigned")) comparator_4 (
    .a(REGNO1), .b(WrREG_MEM), .eq(REGNO1___WrREG_MEM));  // open: gt, lt
  Comparator #(.width(4), .mode("unsigned")) comparator_5 (
    .a(REGNO1), .b(WrREG_WB), .eq(REGNO1___WrREG_WB));  // open: gt, lt
  Comparator #(.width(4), .mode("unsigned")) comparator_6 (
    .a(REGNO2), .b(WrREG_EX), .eq(REGNO2___WrREG_EX));  // open: gt, lt
  Comparator #(.width(4), .mode("unsigned")) comparator_7 (
    .a(REGNO2), .b(WrREG_MEM), .eq(REGNO2___WrREG_MEM));  // open: gt, lt
  Comparator #(.width(4), .mode("unsigned")) comparator_8 (
    .a(REGNO2), .b(WrREG_WB), .eq(REGNO2___WrREG_WB));  // open: gt, lt
  Comparator #(.width(3), .mode("unsigned")) comparator_9 (.a(Opcode_EX), .b(3'b111), .eq(Op_EX___7));  // open: gt, lt
  Comparator #(.width(3), .mode("unsigned")) comparator_10 (
    .a(Opcode_MEM), .b(3'b111), .eq(Op_MEM___7));  // open: gt, lt
  Comparator #(.width(3), .mode("unsigned")) comparator_11 (.a(Opcode_WB), .b(3'b111), .eq(Op_WB___7));  // open: gt, lt
  ROM #(.addrWidth(3), .dataWidth(1)) rom_1 (.addr(Opcode_EX), .data(Src_EX));  // open: sel
  ROM #(.addrWidth(3), .dataWidth(2)) rom_2 (.addr(Opcode_MEM), .data(Src_MEM));  // open: sel
  ROM #(.addrWidth(3), .dataWidth(2)) rom_3 (.addr(Opcode_WB), .data(Src_WB));  // open: sel
  Multiplexer #(.width(32)) multiplexer_1 (.in0(EX_ALU), .in1(EX_PC_1), .out(Data_From_EX), .sel(Src_EX), .en(1'b1));
  Multiplexer #(.select(2), .width(32)) multiplexer_2 (
    .in0(MEM_ALU), .in1(MEM_Data), .in2(MEM_PC_1), .out(Data_From_MEM), .sel(Src_MEM), .en(1'b1));  // open: in3
  Multiplexer #(.select(2), .width(32)) multiplexer_3 (
    .in0(WB_ALU), .in1(WB_MEM), .in2(WB_PC_1), .out(Data_From_WB), .sel(Src_WB), .en(1'b1));  // open: in3
  or or_1 (or_1_out, Op_EX___7, Op_EX___4);
  Comparator #(.width(3), .mode("unsigned")) comparator_12 (
    .a(Opcode_EX), .b(3'b011), .eq(comparator_12_eq));  // open: gt, lt
  not not_1 (not_1_out, comparator_12_eq);
  not not_2 (not_2_out, comparator_13_eq);
  Comparator #(.width(3), .mode("unsigned")) comparator_13 (
    .a(Opcode_EX), .b(3'b011), .eq(comparator_13_eq));  // open: gt, lt
  or or_2 (or_2_out, Op_EX___7, Op_EX___4, not_3_out);
  not not_3 (not_3_out, REGNO1___WrREG_EX);
  or or_3 (or_3_out, Op_EX___7, Op_EX___4, not_4_out);
  not not_4 (not_4_out, REGNO1___WrREG_EX);
  or or_4 (or_4_out, Op_MEM___7, Op_MEM___4, not_5_out);
  not not_5 (not_5_out, REGNO1___WrREG_MEM);
  Comparator #(.width(3), .mode("unsigned")) comparator_14 (.a(Opcode_EX), .b(3'b100), .eq(Op_EX___4));  // open: gt, lt
  Comparator #(.width(3), .mode("unsigned")) comparator_15 (
    .a(Opcode_MEM), .b(3'b100), .eq(Op_MEM___4));  // open: gt, lt
  Comparator #(.width(3), .mode("unsigned")) comparator_16 (.a(Opcode_WB), .b(3'b100), .eq(Op_WB___4));  // open: gt, lt
  and and_1 (and_1_out, REGNO1_W__EX, not_1_out);
  and and_2 (and_2_out, REGNO2_W__EX, not_2_out);
  not not_6 (not_6_out, REGNO1___0);
  not not_7 (not_7_out, Op_MEM___7);
  not not_8 (not_8_out, REGNO1___0);
  or or_5 (or_5_out, Op_EX___7, Op_EX___4);
  not not_9 (not_9_out, REGNO2___WrREG_EX);
  not not_10 (not_10_out, REGNO2___WrREG_EX);
  not not_11 (not_11_out, REGNO2___WrREG_MEM);
  not not_12 (not_12_out, REGNO1___0);
  and and_3 (REGNO1_W__EX, not_12_out, REGNO1___WrREG_EX, not_13_out);
  not not_13 (not_13_out, or_1_out);
  and and_4 (REGNO1_W__MEM, not_6_out, or_2_out, REGNO1___WrREG_MEM, not_7_out);
  and and_5 (REGNO1_W__WB, not_8_out, or_3_out, or_4_out, REGNO1___WrREG_WB, Op_WB___7);
  or or_6 (or_6_out, Op_EX___7, Op_EX___4, not_9_out);
  or or_7 (or_7_out, Op_EX___7, Op_EX___4, not_10_out);
  or or_8 (or_8_out, Op_MEM___7, Op_MEM___4, not_11_out);
  or or_9 (Replace_REGNO1, and_1_out, REGNO1_W__MEM, REGNO1_W__WB);
  or or_10 (Replace_REGNO2, and_2_out, REGNO2_W__MEM, REGNO2_W__WB);
  assign Data_For_REGNO1 = REGNO1_W__EX ? Data_From_EX : 32'bz;  // Controlled_Buffer controlled_buffer_1
  assign Data_For_REGNO1 = REGNO1_W__MEM ? Data_From_MEM : 32'bz;  // Controlled_Buffer controlled_buffer_2
  assign Data_For_REGNO1 = REGNO1_W__WB ? Data_From_WB : 32'bz;  // Controlled_Buffer controlled_buffer_3
  not not_14 (not_14_out, REGNO2___0);
  not not_15 (not_15_out, or_5_out);
  not not_16 (not_16_out, REGNO2___0);
  not not_17 (not_17_out, Op_MEM___7);
  not not_18 (not_18_out, REGNO2___0);
  nor nor_1 (nor_1_out, REGNO1_W__EX, REGNO1_W__MEM, REGNO1_W__WB);
  and and_6 (REGNO2_W__EX, not_14_out, REGNO2___WrREG_EX, not_15_out);
  assign Data_For_REGNO2 = REGNO2_W__EX ? Data_From_EX : 32'bz;  // Controlled_Buffer controlled_buffer_4
  and and_7 (REGNO2_W__MEM, not_16_out, or_6_out, REGNO2___WrREG_MEM, not_17_out);
  assign Data_For_REGNO2 = REGNO2_W__MEM ? Data_From_MEM : 32'bz;  // Controlled_Buffer controlled_buffer_5
  and and_8 (REGNO2_W__WB, not_18_out, or_7_out, or_8_out, REGNO2___WrREG_WB, Op_WB___7);
  assign Data_For_REGNO2 = REGNO2_W__WB ? Data_From_WB : 32'bz;  // Controlled_Buffer controlled_buffer_6
  assign Data_For_REGNO1 = nor_1_out ? {32{1'b0}} : 32'bz;  // Controlled_Buffer controlled_buffer_7
  nor nor_2 (nor_2_out, REGNO2_W__EX, REGNO2_W__MEM, REGNO2_W__WB);
  assign Data_For_REGNO2 = nor_2_out ? {32{1'b0}} : 32'bz;  // Controlled_Buffer controlled_buffer_8

  // Notes on the sheet:
  //   contents of rom_1 (hex, n*v repeats v):
  //   6*0 1
  //   contents of rom_2 (hex, n*v repeats v):
  //   0 0 0 1 0 0 2
  //   contents of rom_3 (hex, n*v repeats v):
  //   0 0 0 1 0 0 2
endmodule
