// Logisim project lastname_firstname.circ as structural Verilog: 11 circuits, main circuit main
module main (
  output [31:0] CheckA,
  output [3:0] CheckA_2
);

  wire and_1_out, and_2_out, and_3_out, B, CheckA_t, CheckB, Clock, comparator_1_eq, comparator_2_eq,
       comparator_3_eq, comparator_4_eq, comparator_5_eq, comparator_6_eq, ex_mem_buffer_1_ldmem_out,
       ex_mem_buffer_1_wrmem_out, idrr_ex_buffer_1_jump_out, idrr_ex_buffer_1_ldmem_out,
       idrr_ex_buffer_1_wrmem_out, idrr_ex_buffer_1_wrreg_out, Jump, Jumping, not_1_out, not_2_out, or_1_out,
       or_2_out, Reg2Read, RegToWr, Stall, StallR, WrEN;
  wire [0:0] ex_mem_buffer_1_wrreg_out;
  wire [1:0] ex_mem_buffer_1_datatowr_out, Func, idrr_ex_buffer_1_datatowr_out, idrr_ex_buffer_1_func_out,
       mem_wb_buffer_1_datatowr_out, multiplexer_4_out, multiplexer_4_out_3, multiplexer_17_out, NextInst;
  wire [2:0] multiplexer_10_out, Opcode;
  wire [3:0] BToCheck, ex_mem_buffer_1_regtowr_out, idrr_ex_buffer_1_regtowr_out, LWWrReg,
       multiplexer_12_out, RegToWr_In, Rx, Ry, Rz, WrREGNO;
  wire [8:5] multiplexer_4_out_2;
  wire [10:0] rom_2_data;
  wire [31:0] adder_1_out, alu_1_out, BEQ, bit_extender_1_out, dual_ported_register_file_1_out1,
       dual_ported_register_file_1_out2, ex_mem_buffer_1_alu_out, ex_mem_buffer_1_datatowrmem_out,
       ex_mem_buffer_1_pc_out, idrr_ex_buffer_1_a_out, idrr_ex_buffer_1_b_out, idrr_ex_buffer_1_off_out,
       idrr_ex_buffer_1_pc_out, idrr_ex_buffer_1_rx_contents_out, if_idrr_buffer_1_instruction_out,
       if_idrr_buffer_1_pc_out, INPUT, JALR, mem_wb_buffer_1_alu_out, mem_wb_buffer_1_d_mem_out,
       mem_wb_buffer_1_pc_out, multiplexer_1_out, multiplexer_8_out, multiplexer_13_out, multiplexer_14_out,
       multiplexer_18_out, multiplexer_20_out, PC, ram_1_data, rom_1_data;
  wire [31:4] multiplexer_2_out;

  Register #(.width(32)) u_PC (.D(multiplexer_1_out), .en(not_1_out), .Q(CheckA), .clk(Clock));  // open: clr
  not not_1 (not_1_out, Stall);
  Clock clock_1 (.out(Clock));
  Multiplexer #(.select(2), .width(32)) multiplexer_1 (
    .in0(adder_1_out), .in1(BEQ), .in2(JALR), .out(multiplexer_1_out), .sel(NextInst), .en(1'b1));  // open: in3
  Adder #(.width(32)) adder_1 (.a(CheckA), .b(32'h1), .out(adder_1_out));  // open: cin, cout
  ROM #(.addrWidth(24), .dataWidth(32)) rom_1 (.addr(CheckA[23:0]), .data(rom_1_data));  // open: sel
  IF_IDRR_Buffer if_idrr_buffer_1 (
    .Instruction_In(rom_1_data), .PC_In(adder_1_out), .Instruction_Out(if_idrr_buffer_1_instruction_out),
    .PC_Out(if_idrr_buffer_1_pc_out), .Clock(Clock), .StallBit(Stall));
  Comparator #(.width(32)) comparator_1 (
    .a({multiplexer_2_out[31], Opcode, Rx, Ry, multiplexer_2_out[19:4], Rz}), .b({32{1'b0}}),
    .eq(comparator_1_eq));  // open: gt, lt
  Multiplexer #(.width(32)) multiplexer_2 (
    .in0(if_idrr_buffer_1_instruction_out), .in1({32{1'b0}}),
    .out({multiplexer_2_out[31], Opcode, Rx, Ry, multiplexer_2_out[19:4], Rz}), .sel(Jumping), .en(1'b1));
  Multiplexer #(.width(32)) multiplexer_3 (
    .in0(if_idrr_buffer_1_pc_out), .in1({32{1'b0}}), .out(PC), .sel(Jumping), .en(1'b1));
  Multiplexer #(.width(11)) multiplexer_4 (
    .in0(rom_2_data), .in1({11{1'b0}}),
    .out({multiplexer_4_out_3, multiplexer_4_out_2, multiplexer_4_out, RegToWr, B, Reg2Read}),
    .sel(comparator_1_eq), .en(1'b1));
  ROM #(.addrWidth(3), .dataWidth(11)) rom_2 (.addr(Opcode), .data(rom_2_data));  // open: sel
  Stalling_Unit stalling_unit_1 (.OpCodeIn(Opcode), .CheckA(CheckA_t), .CheckB(CheckB));
  Multiplexer #(.width(4)) multiplexer_5 (.in0(Rx), .in1(Rz), .out(BToCheck), .sel(Reg2Read), .en(1'b1));
  Comparator #(.width(3)) comparator_2 (.a(Opcode), .b(3'b011), .eq(comparator_2_eq));  // open: gt, lt
  assign bit_extender_1_out = {{12{multiplexer_2_out[19]}}, {multiplexer_2_out[19:4], Rz}};  // Bit_Extender bit_extender_1
  Multiplexer #(.width(4)) multiplexer_6 (.in0(Rx), .in1(Ry), .out(RegToWr_In), .sel(RegToWr), .en(1'b1));
  Multiplexer #(.width(4)) multiplexer_7 (.in0(4'b0000), .in1(Rx), .out(CheckA_2), .sel(comparator_2_eq), .en(1'b1));
  Register #(.width(4)) register_1 (.D(CheckA_2), .en(1'b1), .Q(LWWrReg), .clk(Clock));  // open: clr
  Comparator #(.width(4)) comparator_3 (.a(LWWrReg), .b(4'b0000), .eq(comparator_3_eq));  // open: gt, lt
  Dual_Ported_Register_File dual_ported_register_file_1 (
    .CLK(Clock), .WrREGNO(WrREGNO), .RdREGNO1(Ry), .RdREGNO2(BToCheck), .INPUT(INPUT),
    .OUT1(dual_ported_register_file_1_out1), .OUT2(dual_ported_register_file_1_out2), .WrEN(WrEN));
  Comparator #(.width(4), .mode("unsigned")) comparator_4 (.a(Ry), .b(LWWrReg), .eq(comparator_4_eq));  // open: gt, lt
  Comparator #(.width(4), .mode("unsigned")) comparator_5 (
    .a(BToCheck), .b(LWWrReg), .eq(comparator_5_eq));  // open: gt, lt
  buf or_1 (or_1_out, StallR);  // OR_Gate
  Multiplexer #(.width(32)) multiplexer_8 (
    .in0(dual_ported_register_file_1_out2), .in1(bit_extender_1_out), .out(multiplexer_8_out), .sel(B),
    .en(1'b1));
  and and_1 (and_1_out, comparator_4_eq, CheckA_t);
  and and_2 (and_2_out, comparator_5_eq, CheckB);
  IDRR_EX_Buffer idrr_ex_buffer_1 (
    .Clock(Clock), .LdMem_In(multiplexer_4_out_2[6]), .LdMem_Out(idrr_ex_buffer_1_ldmem_out),
    .WrMem_In(multiplexer_4_out_2[7]), .WrMem_Out(idrr_ex_buffer_1_wrmem_out),
    .WrReg_In(multiplexer_4_out_2[8]), .WrReg_Out(idrr_ex_buffer_1_wrreg_out),
    .DataToWr_In(multiplexer_4_out_3), .DataToWr_Out(idrr_ex_buffer_1_datatowr_out), .RegToWr_In(RegToWr_In),
    .RegToWr_Out(idrr_ex_buffer_1_regtowr_out), .A_In(dual_ported_register_file_1_out1),
    .A_Out(idrr_ex_buffer_1_a_out), .Rx_Contents_In(dual_ported_register_file_1_out2),
    .Rx_Contents_Out(idrr_ex_buffer_1_rx_contents_out), .PC_In(PC), .PC_Out(idrr_ex_buffer_1_pc_out),
    .B_In(multiplexer_8_out), .B_Out(idrr_ex_buffer_1_b_out), .Jump_In(multiplexer_4_out_2[5]),
    .Jump_Out(idrr_ex_buffer_1_jump_out), .Func_In(multiplexer_4_out), .Func_Out(idrr_ex_buffer_1_func_out),
    .Off_In(bit_extender_1_out), .Off_Out(idrr_ex_buffer_1_off_out), .StallBit(Stall));
  or or_2 (or_2_out, and_1_out, and_2_out);
  and and_3 (and_3_out, or_2_out, not_2_out);
  not not_2 (not_2_out, comparator_3_eq);
  Multiplexer #(.width(2)) multiplexer_9 (
    .in0(idrr_ex_buffer_1_func_out), .in1(2'b00), .out(Func), .sel(or_1_out), .en(1'b1));
  Multiplexer multiplexer_10 (
    .in0(idrr_ex_buffer_1_ldmem_out), .in1(1'b0), .out(multiplexer_10_out[0]), .sel(or_1_out), .en(1'b1));
  Multiplexer multiplexer_11 (
    .in0(idrr_ex_buffer_1_wrreg_out), .in1(1'b0), .out(multiplexer_10_out[2]), .sel(or_1_out), .en(1'b1));
  Multiplexer #(.width(4)) multiplexer_12 (
    .in0(idrr_ex_buffer_1_regtowr_out), .in1(4'b0000), .out(multiplexer_12_out), .sel(or_1_out), .en(1'b1));
  Multiplexer #(.width(32)) multiplexer_13 (
    .in0(idrr_ex_buffer_1_b_out), .in1({32{1'b0}}), .out(multiplexer_13_out), .sel(or_1_out), .en(1'b1));
  Multiplexer #(.width(32)) multiplexer_14 (
    .in0(idrr_ex_buffer_1_pc_out), .in1({32{1'b0}}), .out(multiplexer_14_out), .sel(or_1_out), .en(1'b1));
  Register #(.width(1), .trigger("falling")) register_2 (
    .D(and_3_out), .en(1'b1), .Q(Stall), .clk(Clock));  // open: clr
  Multiplexer multiplexer_15 (.in0(idrr_ex_buffer_1_jump_out), .in1(1'b0), .out(Jump), .sel(or_1_out), .en(1'b1));
  Multiplexer multiplexer_16 (
    .in0(idrr_ex_buffer_1_wrmem_out), .in1(1'b0), .out(multiplexer_10_out[1]), .sel(or_1_out), .en(1'b1));
  Multiplexer #(.width(2)) multiplexer_17 (
    .in0(idrr_ex_buffer_1_datatowr_out), .in1(2'b00), .out(multiplexer_17_out), .sel(or_1_out), .en(1'b1));
  Multiplexer #(.width(32)) multiplexer_18 (
    .in0(idrr_ex_buffer_1_a_out), .in1({32{1'b0}}), .out(multiplexer_18_out), .sel(or_1_out), .en(1'b1));
  Multiplexer #(.width(32)) multiplexer_19 (
    .in0(idrr_ex_buffer_1_rx_contents_out), .in1({32{1'b0}}), .out(JALR), .sel(or_1_out), .en(1'b1));
  Multiplexer #(.width(32)) multiplexer_20 (
    .in0(idrr_ex_buffer_1_off_out), .in1({32{1'b0}}), .out(multiplexer_20_out), .sel(or_1_out), .en(1'b1));
  Register #(.width(1)) register_3 (.D(and_3_out), .en(1'b1), .Q(StallR), .clk(Clock));  // open: clr
  Adder #(.width(32)) adder_2 (.a(multiplexer_14_out), .b(multiplexer_20_out), .out(BEQ));  // open: cin, cout
  Next_Instruction next_instruction_1 (._0(comparator_6_eq), .Func(Func), .Jump(Jump), .NextInst(NextInst));
  Comparator #(.width(32)) comparator_6 (.a(alu_1_out), .b({32{1'b0}}), .eq(comparator_6_eq));  // open: gt, lt
  ALU alu_1 (.FUNC(Func), .A(multiplexer_18_out), .B(multiplexer_13_out), .OUT(alu_1_out));
  Comparator #(.width(2), .mode("unsigned")) comparator_7 (.a(NextInst), .b(2'b00), .gt(Jumping));  // open: eq, lt
  EX_MEM_Buffer ex_mem_buffer_1 (
    .LdMem_In(multiplexer_10_out[0]), .WrMem_In(multiplexer_10_out[1]), .WrReg_In(multiplexer_10_out[2]),
    .DataToWr_In(multiplexer_17_out), .RegToWr_In(multiplexer_12_out), .ALU_In(alu_1_out),
    .DataToWrMem_In(JALR), .PC_In(multiplexer_14_out), .LdMem_Out(ex_mem_buffer_1_ldmem_out),
    .WrMem_Out(ex_mem_buffer_1_wrmem_out), .WrReg_Out(ex_mem_buffer_1_wrreg_out[0]),
    .DataToWr_Out(ex_mem_buffer_1_datatowr_out), .RegToWr_Out(ex_mem_buffer_1_regtowr_out),
    .ALU_Out(ex_mem_buffer_1_alu_out), .DataToWrMem_Out(ex_mem_buffer_1_datatowrmem_out),
    .PC_Out(ex_mem_buffer_1_pc_out), .Clock(Clock));
  RAM #(.addrWidth(24), .dataWidth(32), .bus("separate")) ram_1 (
    .addr(ex_mem_buffer_1_alu_out[23:0]), .din(ex_mem_buffer_1_datatowrmem_out), .data(ram_1_data),
    .str(ex_mem_buffer_1_wrmem_out), .clk(Clock), .ld(ex_mem_buffer_1_ldmem_out));  // open: sel, clr
  MEM_WB_Buffer mem_wb_buffer_1 (
    .WrReg_In(ex_mem_buffer_1_wrreg_out[0]), .DataToWr_In(ex_mem_buffer_1_datatowr_out),
    .RegToWr_In(ex_mem_buffer_1_regtowr_out), .ALU_In(ex_mem_buffer_1_alu_out), .D_MEM_In(ram_1_data),
    .WrReg_Out(WrEN), .DataToWr_Out(mem_wb_buffer_1_datatowr_out), .RegToWr_Out(WrREGNO),
    .ALU_Out(mem_wb_buffer_1_alu_out), .D_MEM_Out(mem_wb_buffer_1_d_mem_out), .Clock(Clock),
    .PC_In(ex_mem_buffer_1_pc_out), .PC_Out(mem_wb_buffer_1_pc_out));
  Multiplexer #(.select(2), .width(32)) multiplexer_21 (
    .in0(mem_wb_buffer_1_alu_out), .in1(mem_wb_buffer_1_d_mem_out), .in2(mem_wb_buffer_1_pc_out),
    .out(INPUT), .sel(mem_wb_buffer_1_datatowr_out), .en(1'b1));  // open: in3

  // Notes on the sheet:
  //   contents of rom_1 (hex, n*v repeats v):
  //   23000007 4*0 2800000b 4*0 68f00000 4*0 4300003
  //   contents of rom_2 (hex, n*v repeats v):
  //   101 109 102 342 82 10 524
endmodule

module Dual_Ported_Register_File (
  input  CLK,
  input  WrEN,
  input  [3:0] WrREGNO,
  input  [3:0] RdREGNO1,
  input  [3:0] RdREGNO2,
  input  [31:0] INPUT,
  output [31:0] OUT1,
  output [31:0] OUT2
);

  wire En_a0, En_a1, En_a2, En_a3, En_a4, En_at, En_fp, En_k0, En_ra, En_s0, En_s1, En_s2, En_s3, En_sp,
       En_v0;
  wire [31:0] a0, a1, a2, a3, a4, at, fp, k0, ra, s0, s1, s2, s3, sp, v0, zero;

  Decoder #(.select(4), .disabled(0)) decoder_1 (
    .out1(En_at), .out2(En_v0), .out3(En_a0), .out4(En_a1), .out5(En_a2), .out6(En_a3), .out7(En_a4),
    .out8(En_s0), .out9(En_s1), .out10(En_s2), .out11(En_s3), .out12(En_k0), .out13(En_sp), .out14(En_fp),
    .out15(En_ra), .sel(WrREGNO), .en(WrEN));  // open: out0
  Register #(.width(32)) u_zero (.D(INPUT), .en(1'b0), .Q(zero), .clk(CLK));  // open: clr
  Register #(.width(32)) u_at (.D(INPUT), .en(En_at), .Q(at), .clk(CLK));  // open: clr
  Register #(.width(32)) u_v0 (.D(INPUT), .en(En_v0), .Q(v0), .clk(CLK));  // open: clr
  Register #(.width(32)) u_a0 (.D(INPUT), .en(En_a0), .Q(a0), .clk(CLK));  // open: clr
  Register #(.width(32)) u_a1 (.D(INPUT), .en(En_a1), .Q(a1), .clk(CLK));  // open: clr
  Register #(.width(32)) u_a2 (.D(INPUT), .en(En_a2), .Q(a2), .clk(CLK));  // open: clr
  Register #(.width(32)) u_a3 (.D(INPUT), .en(En_a3), .Q(a3), .clk(CLK));  // open: clr
  Register #(.width(32)) u_a4 (.D(INPUT), .en(En_a4), .Q(a4), .clk(CLK));  // open: clr
  Multiplexer #(.select(4), .width(32), .disabled(0), .enable("false")) multiplexer_1 (
    .in0(zero), .in1(at), .in2(v0), .in3(a0), .in4(a1), .in5(a2), .in6(a3), .in7(a4), .in8(s0), .in9(s1),
    .in10(s2), .in11(s3), .in12(k0), .in13(sp), .in14(fp), .in15(ra), .out(OUT2), .sel(RdREGNO2));
  Register #(.width(32)) u_s0 (.D(INPUT), .en(En_s0), .Q(s0), .clk(CLK));  // open: clr
  Register #(.width(32)) u_s1 (.D(INPUT), .en(En_s1), .Q(s1), .clk(CLK));  // open: clr
  Register #(.width(32)) u_s2 (.D(INPUT), .en(En_s2), .Q(s2), .clk(CLK));  // open: clr
  Register #(.width(32)) u_s3 (.D(INPUT), .en(En_s3), .Q(s3), .clk(CLK));  // open: clr
  Register #(.width(32)) u_k0 (.D(INPUT), .en(En_k0), .Q(k0), .clk(CLK));  // open: clr
  Register #(.width(32)) u_sp (.D(INPUT), .en(En_sp), .Q(sp), .clk(CLK));  // open: clr
  Register #(.width(32)) u_fp (.D(INPUT), .en(En_fp), .Q(fp), .clk(CLK));  // open: clr
  Register #(.width(32)) u_ra (.D(INPUT), .en(En_ra), .Q(ra), .clk(CLK));  // open: clr
  Multiplexer #(.select(4), .width(32), .disabled(0), .enable("false")) multiplexer_2 (
    .in0(zero), .in1(at), .in2(v0), .in3(a0), .in4(a1), .in5(a2), .in6(a3), .in7(a4), .in8(s0), .in9(s1),
    .in10(s2), .in11(s3), .in12(k0), .in13(sp), .in14(fp), .in15(ra), .out(OUT1), .sel(RdREGNO1));

  // Notes on the sheet:
  //   MODIFY AT YOUR OWN RISK
endmodule

module IF_IDRR_Buffer (
  input  [31:0] Instruction_In,
  input  StallBit,
  input  Clock,
  input  [31:0] PC_In,
  output [31:0] Instruction_Out,
  output [31:0] PC_Out
);

  wire not_1_out;

  not not_1 (not_1_out, StallBit);
  Register #(.width(32)) register_1 (
    .D(Instruction_In), .en(not_1_out), .Q(Instruction_Out), .clk(Clock));  // open: clr
  Register #(.width(32)) register_2 (.D(PC_In), .en(not_1_out), .Q(PC_Out), .clk(Clock));  // open: clr
endmodule

module IDRR_EX_Buffer (
  input  Clock,
  input  [1:0] Func_In,
  input  Jump_In,
  input  LdMem_In,
  input  WrMem_In,
  input  StallBit,
  input  WrReg_In,
  input  [1:0] DataToWr_In,
  input  [3:0] RegToWr_In,
  input  [31:0] A_In,
  input  [31:0] B_In,
  input  [31:0] Rx_Contents_In,
  input  [31:0] PC_In,
  input  [31:0] Off_In,
  output [1:0] Func_Out,
  output Jump_Out,
  output LdMem_Out,
  output WrMem_Out,
  output WrReg_Out,
  output [1:0] DataToWr_Out,
  output [3:0] RegToWr_Out,
  output [31:0] A_Out,
  output [31:0] B_Out,
  output [31:0] Rx_Contents_Out,
  output [31:0] PC_Out,
  output [31:0] Off_Out
);

  wire not_1_out;

  not not_1 (not_1_out, StallBit);
  Register #(.width(2)) register_1 (.D(Func_In), .en(not_1_out), .Q(Func_Out), .clk(Clock));  // open: clr
  Register #(.width(1)) register_2 (.D(Jump_In), .en(not_1_out), .Q(Jump_Out), .clk(Clock));  // open: clr
  Register #(.width(1)) register_3 (.D(LdMem_In), .en(not_1_out), .Q(LdMem_Out), .clk(Clock));  // open: clr
  Register #(.width(1)) register_4 (.D(WrMem_In), .en(not_1_out), .Q(WrMem_Out), .clk(Clock));  // open: clr
  Register #(.width(1)) register_5 (.D(WrReg_In), .en(not_1_out), .Q(WrReg_Out), .clk(Clock));  // open: clr
  Register #(.width(2)) register_6 (.D(DataToWr_In), .en(not_1_out), .Q(DataToWr_Out), .clk(Clock));  // open: clr
  Register #(.width(4)) register_7 (.D(RegToWr_In), .en(not_1_out), .Q(RegToWr_Out), .clk(Clock));  // open: clr
  Register #(.width(32)) register_8 (.D(A_In), .en(not_1_out), .Q(A_Out), .clk(Clock));  // open: clr
  Register #(.width(32)) register_9 (.D(B_In), .en(not_1_out), .Q(B_Out), .clk(Clock));  // open: clr
  Register #(.width(32)) register_10 (
    .D(Rx_Contents_In), .en(not_1_out), .Q(Rx_Contents_Out), .clk(Clock));  // open: clr
  Register #(.width(32)) register_11 (.D(PC_In), .en(not_1_out), .Q(PC_Out), .clk(Clock));  // open: clr
  Register #(.width(32)) register_12 (.D(Off_In), .en(not_1_out), .Q(Off_Out), .clk(Clock));  // open: clr
endmodule

module EX_MEM_Buffer (
  input  Clock,
  input  LdMem_In,
  input  WrMem_In,
  input  WrReg_In,
  input  [1:0] DataToWr_In,
  input  [3:0] RegToWr_In,
  input  [31:0] ALU_In,
  input  [31:0] DataToWrMem_In,
  input  [31:0] PC_In,
  output LdMem_Out,
  output WrMem_Out,
  output WrReg_Out,
  output [1:0] DataToWr_Out,
  output [3:0] RegToWr_Out,
  output [31:0] ALU_Out,
  output [31:0] DataToWrMem_Out,
  output [31:0] PC_Out
);

  Register #(.width(1)) register_1 (.D(LdMem_In), .en(1'b1), .Q(LdMem_Out), .clk(Clock));  // open: clr
  Register #(.width(1)) register_2 (.D(WrMem_In), .en(1'b1), .Q(WrMem_Out), .clk(Clock));  // open: clr
  Register #(.width(1)) register_3 (.D(WrReg_In), .en(1'b1), .Q(WrReg_Out), .clk(Clock));  // open: clr
  Register #(.width(2)) register_4 (.D(DataToWr_In), .en(1'b1), .Q(DataToWr_Out), .clk(Clock));  // open: clr
  Register #(.width(4)) register_5 (.D(RegToWr_In), .en(1'b1), .Q(RegToWr_Out), .clk(Clock));  // open: clr
  Register #(.width(32)) register_6 (.D(ALU_In), .en(1'b1), .Q(ALU_Out), .clk(Clock));  // open: clr
  Register #(.width(32)) register_7 (.D(DataToWrMem_In), .en(1'b1), .Q(DataToWrMem_Out), .clk(Clock));  // open: clr
  Register #(.width(32)) register_8 (.D(PC_In), .en(1'b1), .Q(PC_Out), .clk(Clock));  // open: clr
endmodule

module MEM_WB_Buffer (
  input  Clock,
  input  WrReg_In,
  input  [1:0] DataToWr_In,
  input  [3:0] RegToWr_In,
  input  [31:0] ALU_In,
  input  [31:0] D_MEM_In,
  input  [31:0] PC_In,
  output WrReg_Out,
  output [1:0] DataToWr_Out,
  output [3:0] RegToWr_Out,
  output [31:0] ALU_Out,
  output [31:0] D_MEM_Out,
  output [31:0] PC_Out
);

  Register #(.width(1)) register_1 (.D(WrReg_In), .en(1'b1), .Q(WrReg_Out), .clk(Clock));  // open: clr
  Register #(.width(2)) register_2 (.D(DataToWr_In), .en(1'b1), .Q(DataToWr_Out), .clk(Clock));  // open: clr
  Register #(.width(4)) register_3 (.D(RegToWr_In), .en(1'b1), .Q(RegToWr_Out), .clk(Clock));  // open: clr
  Register #(.width(32)) register_4 (.D(ALU_In), .en(1'b1), .Q(ALU_Out), .clk(Clock));  // open: clr
  Register #(.width(32)) register_5 (.D(D_MEM_In), .en(1'b1), .Q(D_MEM_Out), .clk(Clock));  // open: clr
  Register #(.width(32)) register_6 (.D(PC_In), .en(1'b1), .Q(PC_Out), .clk(Clock));  // open: clr
endmodule

module ALU (
  input  [1:0] FUNC,
  input  [31:0] A,
  input  [31:0] B,
  output [31:0] OUT
);

  wire [31:0] adder_1_out, adder_2_out, nand_1_out, subtractor_1_out;

  Adder #(.width(32)) adder_1 (.a(A), .b(B), .out(adder_1_out), .cin(1'b0));  // open: cout
  assign nand_1_out = ~(A & B);  // NAND_Gate nand_1, 32 bits wide
  Subtractor #(.width(32)) subtractor_1 (.a(A), .b(B), .out(subtractor_1_out), .bin(1'b0));  // open: bout
  Adder #(.width(32)) adder_2 (.a(A), .b({32{1'b0}}), .out(adder_2_out), .cin(1'b1));  // open: cout
  Multiplexer #(.select(2), .width(32), .disabled(0), .enable("false")) multiplexer_1 (
    .in0(adder_1_out), .in1(nand_1_out), .in2(subtractor_1_out), .in3(adder_2_out), .out(OUT), .sel(FUNC));

  // Notes on the sheet:
  //   MODIFY AT YOUR OWN RISK
endmodule

module Stalling_Unit (
  input  [2:0] OpCodeIn,
  output CheckA,
  output CheckB
);

  wire ADD, ADDI, BEQ, JALR, LW, NAND, SW;

  Comparator #(.width(3), .mode("unsigned")) comparator_1 (.a(OpCodeIn), .b(3'b000), .eq(ADD));  // open: gt, lt
  Comparator #(.width(3), .mode("unsigned")) comparator_2 (.a(OpCodeIn), .b(3'b001), .eq(NAND));  // open: gt, lt
  Comparator #(.width(3), .mode("unsigned")) comparator_3 (.a(OpCodeIn), .b(3'b010), .eq(ADDI));  // open: gt, lt
  Comparator #(.width(3), .mode("unsigned")) comparator_4 (.a(OpCodeIn), .b(3'b011), .eq(LW));  // open: gt, lt
  Comparator #(.width(3), .mode("unsigned")) comparator_5 (.a(OpCodeIn), .b(3'b100), .eq(SW));  // open: gt, lt
  Comparator #(.width(3), .mode("unsigned")) comparator_6 (.a(OpCodeIn), .b(3'b101), .eq(BEQ));  // open: gt, lt
  Comparator #(.width(3), .mode("unsigned")) comparator_7 (.a(OpCodeIn), .b(3'b110), .eq(JALR));  // open: gt, lt
  or or_1 (CheckA, ADD, NAND, ADDI, LW, SW, BEQ);
  or or_2 (CheckB, ADD, NAND, SW, BEQ, JALR);
endmodule

module Next_Instruction (
  input  _0,
  input  [1:0] Func,
  input  Jump,
  output [1:0] NextInst
);

  wire and_1_out, comparator_1_eq, nor_1_out;

  Comparator #(.width(2), .mode("unsigned")) comparator_1 (.a(Func), .b(2'b10), .eq(comparator_1_eq));  // open: gt, lt
  and and_1 (and_1_out, _0, comparator_1_eq);
  nor nor_1 (nor_1_out, and_1_out, Jump);
  assign NextInst = and_1_out ? 2'b01 : 2'bz;  // Controlled_Buffer controlled_buffer_1
  assign NextInst = Jump ? 2'b10 : 2'bz;  // Controlled_Buffer controlled_buffer_2
  assign NextInst = nor_1_out ? 2'b00 : 2'bz;  // Controlled_Buffer controlled_buffer_3
endmodule

module Extra (
  output [31:0] CheckA,
  output [3:0] CheckA_2
);

  wire and_1_out, and_2_out, and_3_out, B, CheckA_t, CheckB, Clock, comparator_1_eq, comparator_2_eq,
       comparator_3_eq, comparator_4_eq, comparator_5_eq, comparator_6_eq, ex_mem_buffer_1_ldmem_out,
       ex_mem_buffer_1_wrmem_out, idrr_ex_buffer_1_jump_out, idrr_ex_buffer_1_ldmem_out,
       idrr_ex_buffer_1_wrmem_out, idrr_ex_buffer_1_wrreg_out, Jump, Jumping, not_1_out, not_2_out, or_1_out,
       or_2_out, Reg2Read, RegToWr, Stall, StallR, WrEN;
  wire [0:0] ex_mem_buffer_1_wrreg_out;
  wire [1:0] ex_mem_buffer_1_datatowr_out, Func, idrr_ex_buffer_1_datatowr_out, idrr_ex_buffer_1_func_out,
       mem_wb_buffer_1_datatowr_out, multiplexer_4_out, multiplexer_4_out_3, multiplexer_17_out, NextInst;
  wire [2:0] multiplexer_10_out, Opcode;
  wire [3:0] BToCheck, ex_mem_buffer_1_regtowr_out, idrr_ex_buffer_1_regtowr_out, LWWrReg,
       multiplexer_12_out, RegToWr_In, Rx, Ry, Rz, WrREGNO;
  wire [8:5] multiplexer_4_out_2;
  wire [10:0] rom_2_data;
  wire [31:0] adder_1_out, alu_1_out, BEQ, bit_extender_1_out, dual_ported_register_file_1_out1,
       dual_ported_register_file_1_out2, ex_mem_buffer_1_alu_out, ex_mem_buffer_1_datatowrmem_out,
       ex_mem_buffer_1_pc_out, idrr_ex_buffer_1_a_out, idrr_ex_buffer_1_b_out, idrr_ex_buffer_1_off_out,
       idrr_ex_buffer_1_pc_out, idrr_ex_buffer_1_rx_contents_out, if_idrr_buffer_1_instruction_out,
       if_idrr_buffer_1_pc_out, INPUT, JALR, mem_wb_buffer_1_alu_out, mem_wb_buffer_1_d_mem_out,
       mem_wb_buffer_1_pc_out, multiplexer_1_out, multiplexer_8_out, multiplexer_13_out, multiplexer_14_out,
       multiplexer_18_out, multiplexer_20_out, PC, ram_1_data, rom_1_data;
  wire [31:4] multiplexer_2_out;

  Register #(.width(32)) u_PC (.D(multiplexer_1_out), .en(not_1_out), .Q(CheckA), .clk(Clock));  // open: clr
  not not_1 (not_1_out, Stall);
  Clock clock_1 (.out(Clock));
  Multiplexer #(.select(2), .width(32)) multiplexer_1 (
    .in0(adder_1_out), .in1(BEQ), .in2(JALR), .out(multiplexer_1_out), .sel(NextInst), .en(1'b1));  // open: in3
  Adder #(.width(32)) adder_1 (.a(CheckA), .b(32'h1), .out(adder_1_out));  // open: cin, cout
  ROM #(.addrWidth(24), .dataWidth(32)) rom_1 (.addr(CheckA[23:0]), .data(rom_1_data));  // open: sel
  IF_IDRR_Buffer if_idrr_buffer_1 (
    .Instruction_In(rom_1_data), .PC_In(adder_1_out), .Instruction_Out(if_idrr_buffer_1_instruction_out),
    .PC_Out(if_idrr_buffer_1_pc_out), .Clock(Clock), .StallBit(Stall));
  Comparator #(.width(32)) comparator_1 (
    .a({multiplexer_2_out[31], Opcode, Rx, Ry, multiplexer_2_out[19:4], Rz}), .b({32{1'b0}}),
    .eq(comparator_1_eq));  // open: gt, lt
  Multiplexer #(.width(32)) multiplexer_2 (
    .in0(if_idrr_buffer_1_instruction_out), .in1({32{1'b0}}),
    .out({multiplexer_2_out[31], Opcode, Rx, Ry, multiplexer_2_out[19:4], Rz}), .sel(Jumping), .en(1'b1));
  Multiplexer #(.width(32)) multiplexer_3 (
    .in0(if_idrr_buffer_1_pc_out), .in1({32{1'b0}}), .out(PC), .sel(Jumping), .en(1'b1));
  Multiplexer #(.width(11)) multiplexer_4 (
    .in0(rom_2_data), .in1({11{1'b0}}),
    .out({multiplexer_4_out_3, multiplexer_4_out_2, multiplexer_4_out, RegToWr, B, Reg2Read}),
    .sel(comparator_1_eq), .en(1'b1));
  ROM #(.addrWidth(3), .dataWidth(11)) rom_2 (.addr(Opcode), .data(rom_2_data));  // open: sel
  Stalling_Unit stalling_unit_1 (.OpCodeIn(Opcode), .CheckA(CheckA_t), .CheckB(CheckB));
  Multiplexer #(.width(4)) multiplexer_5 (.in0(Rx), .in1(Rz), .out(BToCheck), .sel(Reg2Read), .en(1'b1));
  Comparator #(.width(3)) comparator_2 (.a(Opcode), .b(3'b011), .eq(comparator_2_eq));  // open: gt, lt
  assign bit_extender_1_out = {{12{multiplexer_2_out[19]}}, {multiplexer_2_out[19:4], Rz}};  // Bit_Extender bit_extender_1
  Multiplexer #(.width(4)) multiplexer_6 (.in0(Rx), .in1(Ry), .out(RegToWr_In), .sel(RegToWr), .en(1'b1));
  Multiplexer #(.width(4)) multiplexer_7 (.in0(4'b0000), .in1(Rx), .out(CheckA_2), .sel(comparator_2_eq), .en(1'b1));
  Register #(.width(4)) register_1 (.D(CheckA_2), .en(1'b1), .Q(LWWrReg), .clk(Clock));  // open: clr
  Comparator #(.width(4)) comparator_3 (.a(LWWrReg), .b(4'b0000), .eq(comparator_3_eq));  // open: gt, lt
  Dual_Ported_Register_File dual_ported_register_file_1 (
    .CLK(Clock), .WrREGNO(WrREGNO), .RdREGNO1(Ry), .RdREGNO2(BToCheck), .INPUT(INPUT),
    .OUT1(dual_ported_register_file_1_out1), .OUT2(dual_ported_register_file_1_out2), .WrEN(WrEN));
  Comparator #(.width(4), .mode("unsigned")) comparator_4 (.a(Ry), .b(LWWrReg), .eq(comparator_4_eq));  // open: gt, lt
  Comparator #(.width(4), .mode("unsigned")) comparator_5 (
    .a(BToCheck), .b(LWWrReg), .eq(comparator_5_eq));  // open: gt, lt
  Multiplexer #(.width(32)) multiplexer_8 (
    .in0(dual_ported_register_file_1_out2), .in1(bit_extender_1_out), .out(multiplexer_8_out), .sel(B),
    .en(1'b1));
  and and_1 (and_1_out, comparator_4_eq, CheckA_t);
  and and_2 (and_2_out, comparator_5_eq, CheckB);
  IDRR_EX_Buffer idrr_ex_buffer_1 (
    .Clock(Clock), .LdMem_In(multiplexer_4_out_2[6]), .LdMem_Out(idrr_ex_buffer_1_ldmem_out),
    .WrMem_In(multiplexer_4_out_2[7]), .WrMem_Out(idrr_ex_buffer_1_wrmem_out),
    .WrReg_In(multiplexer_4_out_2[8]), .WrReg_Out(idrr_ex_buffer_1_wrreg_out),
    .DataToWr_In(multiplexer_4_out_3), .DataToWr_Out(idrr_ex_buffer_1_datatowr_out), .RegToWr_In(RegToWr_In),
    .RegToWr_Out(idrr_ex_buffer_1_regtowr_out), .A_In(dual_ported_register_file_1_out1),
    .A_Out(idrr_ex_buffer_1_a_out), .Rx_Contents_In(dual_ported_register_file_1_out2),
    .Rx_Contents_Out(idrr_ex_buffer_1_rx_contents_out), .PC_In(PC), .PC_Out(idrr_ex_buffer_1_pc_out),
    .B_In(multiplexer_8_out), .B_Out(idrr_ex_buffer_1_b_out), .Jump_In(multiplexer_4_out_2[5]),
    .Jump_Out(idrr_ex_buffer_1_jump_out), .Func_In(multiplexer_4_out), .Func_Out(idrr_ex_buffer_1_func_out),
    .Off_In(bit_extender_1_out), .Off_Out(idrr_ex_buffer_1_off_out), .StallBit(Stall));
  or or_1 (or_1_out, and_1_out, and_2_out);
  and and_3 (and_3_out, or_1_out, not_2_out);
  not not_2 (not_2_out, comparator_3_eq);
  Multiplexer #(.width(2)) multiplexer_9 (
    .in0(idrr_ex_buffer_1_func_out), .in1(2'b00), .out(Func), .sel(StallR), .en(1'b1));
  Multiplexer multiplexer_10 (
    .in0(idrr_ex_buffer_1_ldmem_out), .in1(1'b0), .out(multiplexer_10_out[0]), .sel(StallR), .en(1'b1));
  Multiplexer multiplexer_11 (
    .in0(idrr_ex_buffer_1_wrreg_out), .in1(1'b0), .out(multiplexer_10_out[2]), .sel(StallR), .en(1'b1));
  Multiplexer #(.width(4)) multiplexer_12 (
    .in0(idrr_ex_buffer_1_regtowr_out), .in1(4'b0000), .out(multiplexer_12_out), .sel(StallR), .en(1'b1));
  Multiplexer #(.width(32)) multiplexer_13 (
    .in0(idrr_ex_buffer_1_b_out), .in1({32{1'b0}}), .out(multiplexer_13_out), .sel(StallR), .en(1'b1));
  Multiplexer #(.width(32)) multiplexer_14 (
    .in0(idrr_ex_buffer_1_pc_out), .in1({32{1'b0}}), .out(multiplexer_14_out), .sel(StallR), .en(1'b1));
  or or_2 (or_2_out, and_3_out, Jumping);
  Register #(.width(1), .trigger("falling")) register_2 (
    .D(and_3_out), .en(1'b1), .Q(Stall), .clk(Clock));  // open: clr
  Multiplexer multiplexer_15 (.in0(idrr_ex_buffer_1_jump_out), .in1(1'b0), .out(Jump), .sel(StallR), .en(1'b1));
  Multiplexer multiplexer_16 (
    .in0(idrr_ex_buffer_1_wrmem_out), .in1(1'b0), .out(multiplexer_10_out[1]), .sel(StallR), .en(1'b1));
  Multiplexer #(.width(2)) multiplexer_17 (
    .in0(idrr_ex_buffer_1_datatowr_out), .in1(2'b00), .out(multiplexer_17_out), .sel(StallR), .en(1'b1));
  Multiplexer #(.width(32)) multiplexer_18 (
    .in0(idrr_ex_buffer_1_a_out), .in1({32{1'b0}}), .out(multiplexer_18_out), .sel(StallR), .en(1'b1));
  Multiplexer #(.width(32)) multiplexer_19 (
    .in0(idrr_ex_buffer_1_rx_contents_out), .in1({32{1'b0}}), .out(JALR), .sel(StallR), .en(1'b1));
  Multiplexer #(.width(32)) multiplexer_20 (
    .in0(idrr_ex_buffer_1_off_out), .in1({32{1'b0}}), .out(multiplexer_20_out), .sel(StallR), .en(1'b1));
  Register #(.width(1)) register_3 (.D(or_2_out), .en(1'b1), .Q(StallR), .clk(Clock));  // open: clr
  Adder #(.width(32)) adder_2 (.a(multiplexer_14_out), .b(multiplexer_20_out), .out(BEQ));  // open: cin, cout
  Next_Instruction next_instruction_1 (._0(comparator_6_eq), .Func(Func), .Jump(Jump), .NextInst(NextInst));
  Comparator #(.width(32)) comparator_6 (.a(alu_1_out), .b({32{1'b0}}), .eq(comparator_6_eq));  // open: gt, lt
  ALU alu_1 (.FUNC(Func), .A(multiplexer_18_out), .B(multiplexer_13_out), .OUT(alu_1_out));
  Comparator #(.width(2), .mode("unsigned")) comparator_7 (.a(NextInst), .b(2'b00), .gt(Jumping));  // open: eq, lt
  EX_MEM_Buffer ex_mem_buffer_1 (
    .LdMem_In(multiplexer_10_out[0]), .WrMem_In(multiplexer_10_out[1]), .WrReg_In(multiplexer_10_out[2]),
    .DataToWr_In(multiplexer_17_out), .RegToWr_In(multiplexer_12_out), .ALU_In(alu_1_out),
    .DataToWrMem_In(JALR), .PC_In(multiplexer_14_out), .LdMem_Out(ex_mem_buffer_1_ldmem_out),
    .WrMem_Out(ex_mem_buffer_1_wrmem_out), .WrReg_Out(ex_mem_buffer_1_wrreg_out[0]),
    .DataToWr_Out(ex_mem_buffer_1_datatowr_out), .RegToWr_Out(ex_mem_buffer_1_regtowr_out),
    .ALU_Out(ex_mem_buffer_1_alu_out), .DataToWrMem_Out(ex_mem_buffer_1_datatowrmem_out),
    .PC_Out(ex_mem_buffer_1_pc_out), .Clock(Clock));
  RAM #(.addrWidth(24), .dataWidth(32), .bus("separate")) ram_1 (
    .addr(ex_mem_buffer_1_alu_out[23:0]), .din(ex_mem_buffer_1_datatowrmem_out), .data(ram_1_data),
    .str(ex_mem_buffer_1_wrmem_out), .clk(Clock), .ld(ex_mem_buffer_1_ldmem_out));  // open: sel, clr
  MEM_WB_Buffer mem_wb_buffer_1 (
    .WrReg_In(ex_mem_buffer_1_wrreg_out[0]), .DataToWr_In(ex_mem_buffer_1_datatowr_out),
    .RegToWr_In(ex_mem_buffer_1_regtowr_out), .ALU_In(ex_mem_buffer_1_alu_out), .D_MEM_In(ram_1_data),
    .WrReg_Out(WrEN), .DataToWr_Out(mem_wb_buffer_1_datatowr_out), .RegToWr_Out(WrREGNO),
    .ALU_Out(mem_wb_buffer_1_alu_out), .D_MEM_Out(mem_wb_buffer_1_d_mem_out), .Clock(Clock),
    .PC_In(ex_mem_buffer_1_pc_out), .PC_Out(mem_wb_buffer_1_pc_out));
  Multiplexer #(.select(2), .width(32)) multiplexer_21 (
    .in0(mem_wb_buffer_1_alu_out), .in1(mem_wb_buffer_1_d_mem_out), .in2(mem_wb_buffer_1_pc_out),
    .out(INPUT), .sel(mem_wb_buffer_1_datatowr_out), .en(1'b1));  // open: in3

  // Notes on the sheet:
  //   contents of rom_1 (hex, n*v repeats v):
  //   23000007 4*0 2800000b 4*0 68f00000 4*0 4300003
  //   contents of rom_2 (hex, n*v repeats v):
  //   101 109 102 342 82 10 524
endmodule

module Forwarding_Unit (
  input  [3:0] RegNO1,
  input  [3:0] RegNO2,
  input  [31:0] ExecData,
  input  [3:0] ExecRegNo,
  input  [31:0] MemData,
  input  [3:0] MemRegNo,
  output EXReg1,
  output [31:0] ExecDataOut,
  output UseMem,
  output [31:0] MemDataOut
);

  wire comparator_1_eq, comparator_2_eq, comparator_3_eq, comparator_4_eq, comparator_5_eq, comparator_6_eq,
       multiplexer_1_out, multiplexer_2_out, multiplexer_3_out, multiplexer_4_out;

  Comparator #(.width(4), .mode("unsigned")) comparator_1 (
    .a(RegNO1), .b(4'b0000), .eq(comparator_1_eq));  // open: gt, lt
  Comparator #(.width(4), .mode("unsigned")) comparator_2 (
    .a(RegNO2), .b(4'b0000), .eq(comparator_2_eq));  // open: gt, lt
  Comparator #(.width(4), .mode("unsigned")) comparator_3 (
    .a(RegNO1), .b(ExecRegNo), .eq(comparator_3_eq));  // open: gt, lt
  Comparator #(.width(4), .mode("unsigned")) comparator_4 (
    .a(RegNO2), .b(ExecRegNo), .eq(comparator_4_eq));  // open: gt, lt
  Comparator #(.width(4), .mode("unsigned")) comparator_5 (
    .a(RegNO1), .b(MemRegNo), .eq(comparator_5_eq));  // open: gt, lt
  Comparator #(.width(4), .mode("unsigned")) comparator_6 (
    .a(RegNO2), .b(MemRegNo), .eq(comparator_6_eq));  // open: gt, lt
  Multiplexer multiplexer_1 (
    .in0(comparator_3_eq), .in1(1'b0), .out(multiplexer_1_out), .sel(comparator_1_eq), .en(1'b1));
  Multiplexer multiplexer_2 (
    .in0(comparator_4_eq), .in1(1'b0), .out(multiplexer_2_out), .sel(comparator_2_eq), .en(1'b1));
  Multiplexer multiplexer_3 (
    .in0(comparator_5_eq), .in1(1'b0), .out(multiplexer_3_out), .sel(comparator_1_eq), .en(1'b1));
  Multiplexer multiplexer_4 (
    .in0(comparator_6_eq), .in1(1'b0), .out(multiplexer_4_out), .sel(comparator_2_eq), .en(1'b1));

  assign ExecDataOut = ExecData;
  assign MemDataOut = MemData;
endmodule
